# Fritzing sketch full-schematic-v0.0.1 (saved by Fritzing 0.9.3b)
breadboards: 1

parts:
  YwRobot_Power_Supply1 = YwRobot Breadboard Power Supply [part_number=545043]
  Part1 = Fingerprint Sensor
  ESP32_-_Back1 = ESP32 - CAM
  FTDI1 = FTDI Friend

nets:
  N1: YwRobot_Power_Supply1.VCC#9, ESP32_-_Back1.5V
  N2: YwRobot_Power_Supply1.GND#13, ESP32_-_Back1.GND#7
  VCC: Part1.VCC, ESP32_-_Back1.3.3V
  N3: Part1.TX, ESP32_-_Back1.GPIO16
  N4: Part1.RX, ESP32_-_Back1.GPIO1_/_TX, FTDI1.RX
  N5: Part1.GND, ESP32_-_Back1.GND#16
  N6: ESP32_-_Back1.GND#12, FTDI1.GND

notes:
  5V
  3.3V
  USB TO TTL

custom parts:
  YwRobot Breadboard Power Supply: The YwRobot Breadboard Power Supply (MB-V2) has two power rails; they can be 5V or 3V3. Power to the module can be provided through the female USB socket or through the A10 (female) 2.1mm power jack.
  Fingerprint Sensor: FINGERPRIN Sensor
  ESP32 - CAM: The ESP32-CAM has a very competitive small-size camera module that can operate independently as a minimum system with a footprint of only 27*40.5*4.5mm and a deep sleep current of up to 6mA.
